// Logisim project Alu (manual).circ as structural Verilog: 17 circuits, main circuit 1 Bit ALU
// 1BIT ALU
module _1_Bit_ALU (
  input  C_In,
  input  A,
  input  B,
  input  D_Invert,
  input  [1:0] ALU_Operation,
  output ALU_Output,
  output C_Out
);

  wire adder_1_out, and_1_out, multiplexer_1_out, not_1_out, or_1_out;

  not not_1 (not_1_out, B);
  Multiplexer #(.enable("false")) multiplexer_1 (.in0(B), .in1(not_1_out), .out(multiplexer_1_out), .sel(D_Invert));
  Adder #(.width(1)) adder_1 (.a(A), .b(multiplexer_1_out), .out(adder_1_out), .cin(C_In), .cout(C_Out));
  and and_1 (and_1_out, A, B);
  or or_1 (or_1_out, A, B);
  Multiplexer #(.select(2)) multiplexer_2 (
    .in0(and_1_out), .in1(or_1_out), .in2(adder_1_out), .in3(adder_1_out), .out(ALU_Output),
    .sel(ALU_Operation));  // open: en
endmodule

module _4_Bit_ALU (
  input  c_in,
  input  [3:0] data_1,
  input  [3:0] data_2,
  input  B_invert,
  input  [1:0] Opcode,
  output [3:0] Result,
  output Zero,
  output Overflow,
  output C_out
);

  wire n1_bit_alu_1_c_out, n1_bit_alu_2_c_out, n1_bit_alu_3_c_out;

  _1_Bit_ALU u_1_bit_alu_1 (
    .C_In(c_in), .A(data_1[0]), .B(data_2[0]), .ALU_Output(Result[0]), .C_Out(n1_bit_alu_1_c_out),
    .ALU_Operation(Opcode), .D_Invert(B_invert));
  _1_Bit_ALU u_1_bit_alu_2 (
    .C_In(n1_bit_alu_1_c_out), .A(data_1[1]), .B(data_2[1]), .ALU_Output(Result[1]),
    .C_Out(n1_bit_alu_2_c_out), .ALU_Operation(Opcode), .D_Invert(B_invert));
  _1_Bit_ALU u_1_bit_alu_3 (
    .C_In(n1_bit_alu_2_c_out), .A(data_1[2]), .B(data_2[2]), .ALU_Output(Result[2]),
    .C_Out(n1_bit_alu_3_c_out), .ALU_Operation(Opcode), .D_Invert(B_invert));
  _1_Bit_ALU u_1_bit_alu_4 (
    .C_In(n1_bit_alu_3_c_out), .A(data_1[3]), .B(data_2[3]), .ALU_Output(Result[3]), .C_Out(C_out),
    .ALU_Operation(Opcode), .D_Invert(B_invert));
  xor xor_1 (Overflow, n1_bit_alu_3_c_out, C_out);
  or or_1 (Zero, Result[0], Result[1], Result[2], Result[3]);
endmodule

// ALU
module _16_bit_ALU (
  input  [15:0] A,
  input  [1:0] Shift_selector,
  input  [15:0] B,
  input  B_invert__CIN,
  input  [1:0] Opp_code,
  output [15:0] Data_out,
  output Zero,
  output Overflow,
  output Cout
);

  wire n4_bit_alu_1_c_out, n4_bit_alu_1_overflow, n4_bit_alu_1_zero, n4_bit_alu_2_c_out,
       n4_bit_alu_2_overflow, n4_bit_alu_2_zero, n4_bit_alu_3_c_out, n4_bit_alu_3_overflow,
       n4_bit_alu_3_zero, n4_bit_alu_4_overflow, n4_bit_alu_4_zero;
  wire [3:0] n4_bit_alu_1_result, n4_bit_alu_2_result, n4_bit_alu_3_result, n4_bit_alu_4_result;
  wire [15:0] bit_shifter_1_output, nor_2_out;

  _4_Bit_ALU u_4_bit_alu_1 (
    .c_in(B_invert__CIN), .data_1(A[3:0]), .data_2(B[3:0]), .B_invert(B_invert__CIN), .Opcode(Opp_code),
    .Result(n4_bit_alu_1_result), .Zero(n4_bit_alu_1_zero), .Overflow(n4_bit_alu_1_overflow),
    .C_out(n4_bit_alu_1_c_out));
  _4_Bit_ALU u_4_bit_alu_2 (
    .c_in(n4_bit_alu_1_c_out), .data_1(A[7:4]), .data_2(B[7:4]), .B_invert(B_invert__CIN), .Opcode(Opp_code),
    .Result(n4_bit_alu_2_result), .Zero(n4_bit_alu_2_zero), .Overflow(n4_bit_alu_2_overflow),
    .C_out(n4_bit_alu_2_c_out));
  _4_Bit_ALU u_4_bit_alu_3 (
    .c_in(n4_bit_alu_2_c_out), .data_1(A[11:8]), .data_2(B[11:8]), .B_invert(B_invert__CIN),
    .Opcode(Opp_code), .Result(n4_bit_alu_3_result), .Zero(n4_bit_alu_3_zero),
    .Overflow(n4_bit_alu_3_overflow), .C_out(n4_bit_alu_3_c_out));
  _4_Bit_ALU u_4_bit_alu_4 (
    .c_in(n4_bit_alu_3_c_out), .data_1(A[15:12]), .data_2(B[15:12]), .B_invert(B_invert__CIN),
    .Opcode(Opp_code), .Result(n4_bit_alu_4_result), .Zero(n4_bit_alu_4_zero),
    .Overflow(n4_bit_alu_4_overflow), .C_out(Cout));
  nor nor_1 (Zero, n4_bit_alu_1_zero, n4_bit_alu_2_zero, n4_bit_alu_3_zero, n4_bit_alu_4_zero);
  xor xor_1 (Overflow, n4_bit_alu_3_overflow, n4_bit_alu_4_overflow);
  assign nor_2_out = ~(A | B);  // NOR_Gate nor_2, 16 bits wide
  Bit_shifter bit_shifter_1 (.Data_In(A), .Output(bit_shifter_1_output), .Bit_to_be_shifted(B));
  Multiplexer #(.select(2), .width(16), .enable("false")) multiplexer_1 (
    .in0({n4_bit_alu_4_result, n4_bit_alu_3_result, n4_bit_alu_2_result, n4_bit_alu_1_result}),
    .in1(nor_2_out), .in2(bit_shifter_1_output), .out(Data_out), .sel(Shift_selector));  // open: in3

  // Notes on the sheet:
  //   Md. Ariful Haque
  //   1722231642
endmodule

module Single_cycle_datapath (
  input  in_1,
  input  [1:0] SLL,
  input  R,
  input  W,
  input  in_5,
  output [15:0] Output,
  output Zero,
  output Overflow,
  output Cout,
  output [15:0] Full_Instruction,
  output [1:0] OP_Code
);

  wire and_1_out, checkequal_1_out, clock, reset, seven_sigment_1_a, seven_sigment_1_b, seven_sigment_1_c,
       seven_sigment_1_d, seven_sigment_1_e, seven_sigment_1_f, seven_sigment_1_g;
  wire [2:0] spliter_1_rs, spliter_1_rt;
  wire [3:0] spliter_1_opp;
  wire [5:0] spliter_1_immidate_rd_fun;
  wire [15:0] adder_1_out, adder_2_out, bit_extender_1_out, memery_1_data_out, n16_bit_alu_1_data_out,
       register_1_q, register_file_16bit_1_read_data_rs, undriven, undriven_2;

  Register #(.width(16)) register_1 (.D(adder_1_out), .Q(register_1_q), .clk(clock), .clr(reset));  // open: en
  Adder #(.width(16)) adder_1 (.a(16'h1), .b(register_1_q), .out(adder_1_out));  // open: cin, cout
  ROM #(.addrWidth(16), .dataWidth(16)) rom_1 (.addr(register_1_q), .data(Full_Instruction));  // open: sel
  Clock clock_1 (.out(clock));
  Button u_Reset (.out(reset));
  Spliter spliter_1 (
    .in_1(Full_Instruction), .rs(spliter_1_rs), .rt(spliter_1_rt), .Opp(spliter_1_opp),
    .Immidate_rd_fun(spliter_1_immidate_rd_fun));  // open: rd, Functionality, Target_All_opp
  Multiplexer #(.width(16), .enable("false")) multiplexer_1 (
    .in0(undriven), .in1(adder_2_out), .sel(checkequal_1_out));  // open: out
  Adder #(.width(16)) adder_2 (.a(undriven), .b(undriven_2), .out(adder_2_out));  // open: cin, cout
  CheckEqual checkequal_1 (.out(checkequal_1_out));  // open: en, co, zero, Jump
  assign bit_extender_1_out = {{10{1'b0}}, spliter_1_immidate_rd_fun};  // Bit_Extender bit_extender_1
  TEMP_CU temp_cu_1 (.in_1(spliter_1_opp), .out_2(OP_Code));
  Seven_sigment seven_sigment_1 (
    .in_1(Output), .a(seven_sigment_1_a), .b(seven_sigment_1_b), .c(seven_sigment_1_c),
    .d(seven_sigment_1_d), .e(seven_sigment_1_e), .f(seven_sigment_1_f), .g(seven_sigment_1_g));
  and and_1 (and_1_out, OP_Code[0], OP_Code[1]);
  _7_Segment_Display u_7_segment_display_1 (
    .g(seven_sigment_1_g), .f(seven_sigment_1_f), .a(seven_sigment_1_a), .b(seven_sigment_1_b),
    .e(seven_sigment_1_e), .d(seven_sigment_1_d), .c(seven_sigment_1_c));  // open: dp
  Register_File_16bit register_file_16bit_1 (
    .Read_Data_RS(register_file_16bit_1_read_data_rs), .Clock(clock), .RS(spliter_1_rs),
    .Write_Register_RD(spliter_1_rt), .Register_Write(in_1), .Write_Data(Output));  // open: Read_Data_RT, RT
  Multiplexer #(.width(16), .enable("false")) multiplexer_2 (
    .in0(memery_1_data_out), .in1(n16_bit_alu_1_data_out), .out(Output), .sel(in_5));
  _16_bit_ALU u_16_bit_alu_1 (
    .A(register_file_16bit_1_read_data_rs), .B(bit_extender_1_out), .B_invert__CIN(and_1_out),
    .Data_out(n16_bit_alu_1_data_out), .Zero(Zero), .Overflow(Overflow), .Cout(Cout), .Opp_code(OP_Code),
    .Shift_selector(SLL));
  Memery memery_1 (
    .Address_in(n16_bit_alu_1_data_out), .Data_out(memery_1_data_out), .Read(R), .Write(W), .Clock(clock));  // open: Data_in
  Multiplexer #(.width(16), .enable("false")) multiplexer_3 ();  // open: in0, in1, out, sel

  // Other names for the same wires on the sheet: SSD[15:0] = Output

  // Notes on the sheet:
  //   Md. Ariful Haque
  //   contents of rom_1 (hex, n*v repeats v):
  //   8042 8042 50 50
endmodule

// RF
module Register_File_16bit (
  input  Clock,
  input  [2:0] RS,
  input  [2:0] RT,
  input  [2:0] Write_Register_RD,
  input  [15:0] Write_Data,
  input  Register_Write,
  output [15:0] Read_Data_RS,
  output [15:0] Read_Data_RT
);

  wire and_1_out, and_2_out, and_3_out, and_4_out, and_5_out, and_6_out, and_7_out, and_8_out,
       decoder_1_out0, decoder_1_out1, decoder_1_out2, decoder_1_out3, decoder_1_out4, decoder_1_out5,
       decoder_1_out6, decoder_1_out7;
  wire [15:0] R0_q, R1_q, R2_q, R3_q, R4_q, R5_q, R6_q, R7_q;

  Decoder #(.select(3), .enable("false")) decoder_1 (
    .out0(decoder_1_out0), .out1(decoder_1_out1), .out2(decoder_1_out2), .out3(decoder_1_out3),
    .out4(decoder_1_out4), .out5(decoder_1_out5), .out6(decoder_1_out6), .out7(decoder_1_out7),
    .sel(Write_Register_RD));
  and and_1 (and_1_out, decoder_1_out0, Register_Write);
  and and_2 (and_2_out, decoder_1_out1, Register_Write);
  and and_3 (and_3_out, decoder_1_out2, Register_Write);
  and and_4 (and_4_out, decoder_1_out3, Register_Write);
  and and_5 (and_5_out, Register_Write, decoder_1_out4);
  and and_6 (and_6_out, Register_Write, decoder_1_out5);
  and and_7 (and_7_out, Register_Write, decoder_1_out6);
  and and_8 (and_8_out, Register_Write, decoder_1_out7);
  Register #(.width(16)) R0 (.D(Write_Data), .en(and_1_out), .Q(R0_q), .clk(Clock));  // open: clr
  Register #(.width(16)) R1 (.D(Write_Data), .en(and_2_out), .Q(R1_q), .clk(Clock));  // open: clr
  Register #(.width(16)) R2 (.D(Write_Data), .en(and_3_out), .Q(R2_q), .clk(Clock));  // open: clr
  Register #(.width(16)) R3 (.D(Write_Data), .en(and_4_out), .Q(R3_q), .clk(Clock));  // open: clr
  Register #(.width(16)) R4 (.D(Write_Data), .en(and_5_out), .Q(R4_q), .clk(Clock));  // open: clr
  Register #(.width(16)) R5 (.D(Write_Data), .en(and_6_out), .Q(R5_q), .clk(Clock));  // open: clr
  Register #(.width(16)) R6 (.D(Write_Data), .en(and_7_out), .Q(R6_q), .clk(Clock));  // open: clr
  Register #(.width(16)) R7 (.D(Write_Data), .en(and_8_out), .Q(R7_q), .clk(Clock));  // open: clr
  Multiplexer #(.select(3), .width(16)) multiplexer_1 (
    .in0(R0_q), .in1(R1_q), .in2(R2_q), .in3(R3_q), .in4(R4_q), .in5(R5_q), .in6(R6_q), .in7(R7_q),
    .out(Read_Data_RS), .sel(RS));  // open: en
  Multiplexer #(.select(3), .width(16)) multiplexer_2 (
    .in0(R0_q), .in1(R1_q), .in2(R2_q), .in3(R3_q), .in4(R4_q), .in5(R5_q), .in6(R6_q), .in7(R7_q),
    .out(Read_Data_RT), .sel(RT));  // open: en
endmodule

// Decoder
module Seven_sigment (
  input  [15:0] in_1,
  output a,
  output b,
  output c,
  output d,
  output e,
  output f,
  output g
);

  wire and_1_out, and_2_out, and_3_out, and_4_out, and_5_out, and_6_out, and_7_out, and_8_out, and_9_out,
       and_10_out, and_11_out, and_12_out, and_13_out, and_14_out, and_15_out, and_16_out, and_17_out,
       and_18_out, and_19_out, and_20_out, and_21_out, and_22_out, and_23_out, not_1_out, not_2_out,
       not_3_out, not_4_out, not_5_out, not_6_out, not_7_out, not_8_out, not_9_out, not_10_out, not_11_out,
       not_12_out, not_13_out, not_14_out, not_15_out, not_16_out, not_17_out, not_18_out, not_19_out,
       not_20_out, not_21_out, not_22_out, not_23_out, not_24_out, not_25_out, not_26_out, not_27_out,
       not_28_out, not_29_out, not_30_out, not_31_out, not_32_out, not_33_out;
  wire [3:0] bit_extender_1_out;

  Bit_Extender #(.in_width(16), .out_width(4)) bit_extender_1 (.in(in_1), .out(bit_extender_1_out));
  not not_1 (not_1_out, bit_extender_1_out[2]);
  not not_2 (not_2_out, bit_extender_1_out[0]);
  not not_3 (not_3_out, bit_extender_1_out[3]);
  not not_4 (not_4_out, bit_extender_1_out[2]);
  not not_5 (not_5_out, bit_extender_1_out[3]);
  not not_6 (not_6_out, bit_extender_1_out[1]);
  not not_7 (not_7_out, bit_extender_1_out[0]);
  not not_8 (not_8_out, bit_extender_1_out[2]);
  not not_9 (not_9_out, bit_extender_1_out[1]);
  not not_10 (not_10_out, bit_extender_1_out[3]);
  not not_11 (not_11_out, bit_extender_1_out[2]);
  not not_12 (not_12_out, bit_extender_1_out[1]);
  not not_13 (not_13_out, bit_extender_1_out[3]);
  not not_14 (not_14_out, bit_extender_1_out[3]);
  not not_15 (not_15_out, bit_extender_1_out[2]);
  not not_16 (not_16_out, bit_extender_1_out[1]);
  not not_17 (not_17_out, bit_extender_1_out[0]);
  not not_18 (not_18_out, bit_extender_1_out[3]);
  not not_19 (not_19_out, bit_extender_1_out[2]);
  not not_20 (not_20_out, bit_extender_1_out[3]);
  not not_21 (not_21_out, bit_extender_1_out[0]);
  not not_22 (not_22_out, bit_extender_1_out[3]);
  not not_23 (not_23_out, bit_extender_1_out[1]);
  not not_24 (not_24_out, bit_extender_1_out[2]);
  not not_25 (not_25_out, bit_extender_1_out[0]);
  not not_26 (not_26_out, bit_extender_1_out[0]);
  not not_27 (not_27_out, bit_extender_1_out[1]);
  not not_28 (not_28_out, bit_extender_1_out[0]);
  not not_29 (not_29_out, bit_extender_1_out[1]);
  not not_30 (not_30_out, bit_extender_1_out[0]);
  not not_31 (not_31_out, bit_extender_1_out[2]);
  not not_32 (not_32_out, bit_extender_1_out[1]);
  not not_33 (not_33_out, bit_extender_1_out[0]);
  and and_1 (and_1_out, not_1_out, not_2_out);
  and and_2 (and_2_out, bit_extender_1_out[2], bit_extender_1_out[0]);
  and and_3 (and_3_out, not_3_out, not_4_out);
  and and_4 (and_4_out, not_5_out, not_6_out, not_7_out);
  and and_5 (and_5_out, not_8_out, not_9_out);
  and and_6 (and_6_out, not_10_out, bit_extender_1_out[1], bit_extender_1_out[0]);
  and and_7 (and_7_out, not_11_out, not_12_out);
  and and_8 (and_8_out, not_13_out, bit_extender_1_out[0]);
  and and_9 (and_9_out, not_14_out, bit_extender_1_out[2]);
  and and_10 (and_10_out, not_15_out, not_16_out, not_17_out);
  and and_11 (and_11_out, not_18_out, not_19_out, bit_extender_1_out[1]);
  and and_12 (and_12_out, not_20_out, bit_extender_1_out[1], not_21_out);
  and and_13 (and_13_out, not_22_out, bit_extender_1_out[2], not_23_out, bit_extender_1_out[0]);
  and and_14 (and_14_out, not_24_out, not_25_out);
  and and_15 (and_15_out, bit_extender_1_out[1], not_26_out);
  and and_16 (and_16_out, bit_extender_1_out[3], bit_extender_1_out[1]);
  and and_17 (and_17_out, bit_extender_1_out[3], bit_extender_1_out[2]);
  and and_18 (and_18_out, not_27_out, not_28_out);
  and and_19 (and_19_out, bit_extender_1_out[2], not_29_out);
  and and_20 (and_20_out, bit_extender_1_out[2], not_30_out);
  and and_21 (and_21_out, not_31_out, bit_extender_1_out[1]);
  and and_22 (and_22_out, bit_extender_1_out[2], not_32_out);
  and and_23 (and_23_out, bit_extender_1_out[2], not_33_out);
  or or_1 (a, and_1_out, bit_extender_1_out[1], and_2_out, bit_extender_1_out[3]);
  or or_2 (b, and_3_out, and_4_out, and_5_out, and_6_out);
  or or_3 (c, and_7_out, and_8_out, and_9_out);
  or or_4 (d, and_10_out, and_11_out, and_12_out, and_13_out);
  or or_5 (e, and_14_out, and_15_out, and_16_out, and_17_out);
  or or_6 (f, and_18_out, and_19_out, and_20_out, bit_extender_1_out[3]);
  or or_7 (g, and_21_out, and_22_out, and_23_out, bit_extender_1_out[3]);
endmodule

// Memory
module Memery (
  input  [15:0] Address_in,
  input  [15:0] Data_in,
  input  Read,
  input  Clock,
  input  Write,
  output [15:0] Data_out
);

  RAM #(.addrWidth(16), .dataWidth(16), .bus("separate")) ram_1 (
    .addr(Address_in), .din(Data_in), .data(Data_out), .str(Write), .clk(Clock), .ld(Read));  // open: sel, clr
endmodule

// Jump
module CheckEqual (
  input  en,
  input  co,
  input  Jump,
  input  zero,
  output out
);

  wire and_1_out, and_2_out, not_1_out, not_2_out, or_1_out;

  not not_1 (not_1_out, co);
  not not_2 (not_2_out, or_1_out);
  or or_1 (or_1_out, Jump, zero);
  and and_1 (and_1_out, en, not_1_out, not_2_out);
  and and_2 (and_2_out, en, co, or_1_out);
  or or_2 (out, and_1_out, and_2_out);
endmodule

// Control Unit
module CONTROL_UNIT (
  input  [3:0] Full_opcode,
  output [1:0] Op_code,
  output RD,
  output RgW,
  output B,
  output C_IN,
  output CU,
  output MR,
  output RegV,
  output MW,
  output En,
  output SLT,
  output j
);

  wire and_3_out, and_4_out, and_5_out, and_6_out, and_7_out, and_8_out, and_9_out, and_10_out, and_11_out,
       and_12_out, and_13_out, and_14_out, and_15_out, and_16_out, and_17_out, and_20_out, and_21_out,
       and_22_out, and_23_out, not_1_out, not_2_out, not_3_out, not_4_out, not_5_out, not_6_out, not_7_out,
       not_8_out, not_9_out, not_10_out, not_11_out, not_12_out, not_13_out, not_14_out, not_15_out,
       not_16_out, not_17_out, not_18_out, not_19_out, not_20_out, not_21_out, not_22_out;

  or or_1 (Op_code[1], Full_opcode[1], Full_opcode[3]);
  not not_1 (not_1_out, Full_opcode[3]);
  not not_2 (not_2_out, Full_opcode[1]);
  not not_3 (not_3_out, Full_opcode[2]);
  not not_4 (not_4_out, Full_opcode[0]);
  not not_5 (not_5_out, Full_opcode[3]);
  not not_6 (not_6_out, Full_opcode[2]);
  not not_7 (not_7_out, Full_opcode[2]);
  not not_8 (not_8_out, Full_opcode[0]);
  not not_9 (not_9_out, Full_opcode[3]);
  not not_10 (not_10_out, Full_opcode[1]);
  not not_11 (not_11_out, Full_opcode[0]);
  not not_12 (not_12_out, Full_opcode[2]);
  not not_13 (not_13_out, Full_opcode[2]);
  not not_14 (not_14_out, Full_opcode[0]);
  not not_15 (not_15_out, Full_opcode[1]);
  and and_1 (MR, Full_opcode[2], Full_opcode[1], Full_opcode[0]);
  not not_16 (not_16_out, Full_opcode[2]);
  not not_17 (not_17_out, Full_opcode[1]);
  not not_18 (not_18_out, Full_opcode[0]);
  not not_19 (not_19_out, Full_opcode[1]);
  not not_20 (not_20_out, Full_opcode[0]);
  not not_21 (not_21_out, Full_opcode[0]);
  and and_2 (j, Full_opcode[3], Full_opcode[2], Full_opcode[0]);
  and and_3 (and_3_out, not_1_out, not_2_out, Full_opcode[0]);
  and and_4 (and_4_out, not_3_out, Full_opcode[0]);
  and and_5 (and_5_out, Full_opcode[3], Full_opcode[1]);
  and and_6 (and_6_out, Full_opcode[3], Full_opcode[2], not_4_out);
  and and_7 (and_7_out, not_5_out, not_6_out);
  or or_2 (RD, and_7_out, and_8_out, and_9_out);
  and and_8 (and_8_out, not_7_out, Full_opcode[1]);
  and and_9 (and_9_out, Full_opcode[3], Full_opcode[0]);
  not not_22 (not_22_out, Full_opcode[3]);
  and and_10 (and_10_out, Full_opcode[1], Full_opcode[0]);
  or or_3 (RgW, not_22_out, and_10_out, and_11_out);
  and and_11 (and_11_out, Full_opcode[2], not_8_out);
  and and_12 (and_12_out, not_9_out, Full_opcode[2]);
  or or_4 (B, and_12_out, and_13_out);
  and and_13 (and_13_out, Full_opcode[3], not_10_out, not_11_out);
  and and_14 (and_14_out, not_12_out, Full_opcode[1], Full_opcode[0]);
  and and_15 (and_15_out, Full_opcode[3], not_13_out, Full_opcode[0]);
  and and_16 (and_16_out, Full_opcode[3], Full_opcode[1]);
  and and_17 (and_17_out, Full_opcode[3], Full_opcode[2], not_14_out);
  and and_18 (CU, Full_opcode[3], not_15_out, Full_opcode[0]);
  and and_19 (MW, Full_opcode[3], not_16_out, not_17_out, not_18_out);
  and and_20 (and_20_out, Full_opcode[3], not_19_out, Full_opcode[0]);
  or or_5 (En, and_20_out, and_21_out);
  and and_21 (and_21_out, Full_opcode[3], Full_opcode[1], not_20_out);
  and and_22 (and_22_out, Full_opcode[3], Full_opcode[1], Full_opcode[0]);
  or or_6 (SLT, and_22_out, and_23_out);
  and and_23 (and_23_out, Full_opcode[3], Full_opcode[2], not_21_out);
  or or_7 (Op_code[0], and_3_out, and_4_out, and_5_out, and_6_out);
  or or_8 (C_IN, and_14_out, and_15_out, and_16_out, and_17_out);
  not not_23 (RegV, MR);
endmodule

module Spliter (
  input  [15:0] in_1,
  output [2:0] rs,
  output [2:0] rt,
  output [2:0] rd,
  output [2:0] Functionality,
  output [3:0] Opp,
  output [5:0] Immidate_rd_fun,
  output [11:0] Target_All_opp
);


  assign Functionality = in_1[2:0];
  assign Immidate_rd_fun = in_1[5:0];
  assign Opp = in_1[15:12];
  assign rd = in_1[5:3];
  assign rs = in_1[11:9];
  assign rt = in_1[8:6];
  assign Target_All_opp = {in_1[8:6], in_1[11:9], in_1[5:0]};
endmodule

module TEMP_CU (
  input  [3:0] in_1,
  output [1:0] out_2
);

  not not_1 (out_2[1], in_1[1]);

  assign out_2[0] = in_1[0];
endmodule

module Bit_shifter (
  input  [15:0] Data_In,
  input  [15:0] Bit_to_be_shifted,
  output [15:0] Output
);

  wire seven_sigment_1_a, seven_sigment_1_b, seven_sigment_1_c, seven_sigment_1_d, seven_sigment_1_e,
       seven_sigment_1_f, seven_sigment_1_g;
  wire [3:0] bit_extender_1_out;

  Bit_Extender #(.in_width(16), .out_width(4)) bit_extender_1 (.in(Bit_to_be_shifted), .out(bit_extender_1_out));
  Shifter #(.width(16)) shifter_1 (.in(Data_In), .\dist (bit_extender_1_out), .out(Output));
  Seven_sigment seven_sigment_1 (
    .in_1(Output), .a(seven_sigment_1_a), .b(seven_sigment_1_b), .c(seven_sigment_1_c),
    .d(seven_sigment_1_d), .e(seven_sigment_1_e), .f(seven_sigment_1_f), .g(seven_sigment_1_g));
  _7_Segment_Display u_7_segment_display_1 (
    .g(seven_sigment_1_g), .f(seven_sigment_1_f), .a(seven_sigment_1_a), .b(seven_sigment_1_b),
    .e(seven_sigment_1_e), .d(seven_sigment_1_d), .c(seven_sigment_1_c));  // open: dp
endmodule

module Inpute (
  input  [7:0] Give_TEN,
  output [15:0] Output,
  output [15:0] Output_2
);

  wire _0_out, _1_out, _2_out, _3_out, _4_out, _5_out, _6_out, _7_out, _8_out, _9_out, Alart_out, Load_out,
       ReSet_out, seven_sigment_1_a, seven_sigment_1_b, seven_sigment_1_c, seven_sigment_1_d,
       seven_sigment_1_e, seven_sigment_1_f, seven_sigment_1_g, seven_sigment_2_a, seven_sigment_2_b,
       seven_sigment_2_c, seven_sigment_2_d, seven_sigment_2_e, seven_sigment_2_f, seven_sigment_2_g;

  Button _1 (.out(_1_out));
  Button _4 (.out(_4_out));
  Button _7 (.out(_7_out));
  Button ReSet (.out(ReSet_out));
  Button _2 (.out(_2_out));
  Button _3 (.out(_3_out));
  Button _5 (.out(_5_out));
  Button _6 (.out(_6_out));
  Button _8 (.out(_8_out));
  Button _9 (.out(_9_out));
  Button _0 (.out(_0_out));
  Button Load (.out(Load_out));
  Button Alart (.out(Alart_out));
  Encoder encoder_1 (
    ._1(_1_out), ._2(_2_out), ._3(_3_out), ._4(_4_out), ._5(_5_out), ._6(_6_out), ._7(_7_out), ._8(_8_out),
    ._9(_9_out), ._0(_0_out), .OK(Load_out), .in_8(Give_TEN), .Set(ReSet_out), .Entered_data(Output),
    .Loded_data(Output_2), .in_2(Alart_out));
  Seven_sigment seven_sigment_1 (
    .in_1(Output), .a(seven_sigment_1_a), .b(seven_sigment_1_b), .c(seven_sigment_1_c),
    .d(seven_sigment_1_d), .e(seven_sigment_1_e), .f(seven_sigment_1_f), .g(seven_sigment_1_g));
  Seven_sigment seven_sigment_2 (
    .in_1(Output_2), .a(seven_sigment_2_a), .b(seven_sigment_2_b), .c(seven_sigment_2_c),
    .d(seven_sigment_2_d), .e(seven_sigment_2_e), .f(seven_sigment_2_f), .g(seven_sigment_2_g));
  _7_Segment_Display u_7_segment_display_1 (
    .g(seven_sigment_1_g), .f(seven_sigment_1_f), .a(seven_sigment_1_a), .b(seven_sigment_1_b),
    .e(seven_sigment_1_e), .d(seven_sigment_1_d), .c(seven_sigment_1_c));  // open: dp
  _7_Segment_Display u_7_segment_display_2 (
    .g(seven_sigment_2_g), .f(seven_sigment_2_f), .a(seven_sigment_2_a), .b(seven_sigment_2_b),
    .e(seven_sigment_2_e), .d(seven_sigment_2_d), .c(seven_sigment_2_c));  // open: dp
endmodule

module Encoder (
  input  _1,
  input  in_2,
  input  _2,
  input  _3,
  input  _4,
  input  _5,
  input  _6,
  input  [7:0] in_8,
  input  _7,
  input  _8,
  input  _9,
  input  _0,
  input  OK,
  input  Set,
  output [15:0] Entered_data,
  output [15:0] Loded_data
);

  wire and_1_out, not_1_out, or_5_out;
  wire [3:0] multiplexer_1_out, or_4_out;
  wire [7:0] digit_holder_1_data;

  or or_1 (or_4_out[3], _8, _9);
  or or_2 (or_4_out[2], _4, _5, _6, _7);
  or or_3 (or_4_out[1], _2, _7, _6, _3);
  or or_4 (or_4_out[0], _9, _3, _1, _5, _7);
  or or_5 (or_5_out, or_4_out[0], or_4_out[1], or_4_out[2], or_4_out[3], _0);
  not not_1 (not_1_out, or_5_out);
  and and_1 (and_1_out, or_4_out[3], or_4_out[2], or_4_out[1], or_4_out[0]);
  Multiplexer #(.width(4)) multiplexer_1 (
    .in0(or_4_out), .in1(4'b1010), .out(multiplexer_1_out), .sel(not_1_out));  // open: en
  Digit_holder digit_holder_1 (
    .Data_In(multiplexer_1_out), .CLK(or_5_out), .Set(in_2), .GIVE_TEN(in_8), .Data(digit_holder_1_data));
  assign Entered_data = {{8{1'b0}}, digit_holder_1_data};  // Bit_Extender bit_extender_1
  Register #(.width(16)) register_1 (.D(Entered_data), .Q(Loded_data), .clk(OK), .clr(Set));  // open: en
endmodule

module clock (
  input  [3:0] in_1,
  output clk
);

  wire not_1_out, not_2_out;

  not not_1 (not_1_out, in_1[3]);
  not not_2 (not_2_out, in_1[1]);
  or or_1 (clk, not_1_out, not_2_out, in_1[2]);
endmodule

module Digit_holder (
  input  [3:0] Data_In,
  input  CLK,
  input  Set,
  input  [7:0] GIVE_TEN,
  output [7:0] Data
);

  wire clock_1_clk, counter_1_tenth, counter_1_unit;
  wire [7:0] bit_extender_1_out, register_1_q, register_2_q;

  clock clock_1 (.in_1(Data_In), .clk(clock_1_clk));
  assign bit_extender_1_out = {{4{1'b0}}, Data_In};  // Bit_Extender bit_extender_1
  Register register_1 (.D(bit_extender_1_out), .en(counter_1_unit), .Q(register_1_q), .clk(clock_1_clk));  // open: clr
  counter counter_1 (.in_1(CLK), .Tenth(counter_1_tenth), .Unit(counter_1_unit), .in_2(Set));
  Register register_2 (.D(bit_extender_1_out), .en(counter_1_tenth), .Q(register_2_q), .clk(clock_1_clk));  // open: clr
  Multiplier multiplier_1 (.a(register_1_q), .b(GIVE_TEN), .out(Data), .cin(register_2_q));  // open: cout
endmodule

// Selector
module counter (
  input  in_1,
  input  in_2,
  output Tenth,
  output Unit
);

  D_Flip_Flop d_ff_1 (.clk(in_1), .D(Tenth), .Q(Unit));  // open: Qn, preset, en, reset
  D_Flip_Flop d_ff_2 (.clk(in_1), .D(Unit), .Q(Tenth), .preset(in_2));  // open: Qn, en, reset
endmodule
